// Logisim project TME1.circ as structural Verilog: 6 circuits, main circuit main
module main (
  input  a,
  input  b,
  output a_ET_NON_b
);

  wire not_1_out;

  not not_1 (not_1_out, b);
  and and_1 (a_ET_NON_b, a, not_1_out);
endmodule

module Ex1_question1 (
  input  a,
  input  b,
  output a_ET_NON_b
);

  wire not_1_out;

  not not_1 (not_1_out, b);
  and and_1 (a_ET_NON_b, a, not_1_out);
endmodule

module Ex1_question2_mon_XOR (
  input  a,
  input  b,
  output a_XOR_b
);

  wire and_1_out, and_2_out, not_1_out, not_2_out;

  not not_1 (not_1_out, b);
  not not_2 (not_2_out, a);
  and and_1 (and_1_out, not_2_out, b);
  and and_2 (and_2_out, a, not_1_out);
  or or_1 (a_XOR_b, and_2_out, and_1_out);
endmodule

module Ex2_mux2 (
  input  e0,
  input  in_2,
  input  e1,
  output out_4
);

  wire and_1_out, and_2_out, not_1_out;

  not not_1 (not_1_out, in_2);
  and and_1 (and_1_out, in_2, e1);
  and and_2 (and_2_out, e0, not_1_out);
  or or_1 (out_4, and_2_out, and_1_out);
endmodule

module mux4 (
  input  e0,
  input  e1,
  input  i1,
  input  i2,
  input  e2,
  input  e3,
  output s
);

  wire ex2_mux2_1_out_4, ex2_mux2_2_out_4;

  Ex2_mux2 ex2_mux2_1 (.e0(e2), .in_2(i2), .e1(e3), .out_4(ex2_mux2_1_out_4));
  Ex2_mux2 ex2_mux2_2 (.e0(e0), .in_2(i2), .e1(e1), .out_4(ex2_mux2_2_out_4));
  Ex2_mux2 ex2_mux2_3 (.e0(ex2_mux2_2_out_4), .in_2(i1), .e1(ex2_mux2_1_out_4), .out_4(s));

  // Notes on the sheet:
  //   1)  Pour 4 = 2**2 entrees, il faut juste utiliser 2 selexteurs en total.
  //   n(i1).(e0.n(i2)   +   e1.i2)  +   i1.(e2.n(i2) + e3.i2)
  //   n(i1).(n(i2).e0   +  i2.e1)  +   i1.(n(i2).e2 + i2.e3)
  //   e0.n(i1).n(i2)   +   e1.n(i1).i2    +   e2.i1.n(i2)      + e3.i1.i2
endmodule

module Ex3 (
  input  [3:0] A,
  input  [3:0] B,
  input  in_3,
  output [3:0] s
);

  wire not_1_out;

  Multiplexer #(.width(4)) multiplexer_1 (.in0(A), .in1(B), .out(s), .sel(not_1_out), .en(in_3));
  not not_1 (not_1_out, in_3);
endmodule
