// Logisim project TME1_ZheHUANG.circ as structural Verilog
module Ex1_Question1 (
  input  a,
  input  b,
  output a_ET_NON_b
);

  wire not_1_out;

  not not_1 (not_1_out, b);
  and and_1 (a_ET_NON_b, a, not_1_out);
endmodule

module mon_xor (
  input  a,
  input  b,
  output out_3
);

  wire a_not_b_out, not_1_out, not_2_out, not_a_b_out;

  not not_1 (not_1_out, a);
  not not_2 (not_2_out, b);
  and not_a_b (not_a_b_out, not_1_out, b);
  and a_not_b (a_not_b_out, a, not_2_out);
  or or_1 (out_3, a_not_b_out, not_a_b_out);

  // Notes on the sheet:
  //   a XOR b = (not a)b + a(not b)
endmodule

module mux2 (
  input  e0,
  input  i,
  input  e1,
  output out_4
);

  wire and_1_out, and_2_out, not_1_out;

  not not_1 (not_1_out, i);
  and and_1 (and_1_out, e0, not_1_out);
  and and_2 (and_2_out, i, e1);
  or or_1 (out_4, and_1_out, and_2_out);

  // Notes on the sheet:
  //   eX2/Q1   s = i*e_1 + (not i)*e_0
endmodule

module Ex3 (
  input  a3,
  input  a2,
  input  a1,
  input  a0,
  input  i,
  input  b3,
  input  b2,
  input  b1,
  input  b0,
  output out_10,
  output out_11,
  output out_12,
  output out_13
);

  mux2 mux2_1 (.e0(a3), .i(i), .e1(b3), .out_4(out_10));
  mux2 mux2_2 (.e0(a2), .i(i), .e1(b2), .out_4(out_11));
  mux2 mux2_3 (.e0(a1), .i(i), .e1(b1), .out_4(out_12));
  mux2 mux2_4 (.e0(a0), .i(i), .e1(b0), .out_4(out_13));
endmodule

module mux4 (
  input  e0,
  input  e1,
  input  e2,
  input  e3,
  input  i1,
  input  i2,
  output out_7
);

  wire mux2_1_out_4, mux2_2_out_4;

  mux2 mux2_1 (.e0(e0), .i(i2), .e1(e1), .out_4(mux2_1_out_4));
  mux2 mux2_2 (.e0(e2), .i(i2), .e1(e3), .out_4(mux2_2_out_4));
  mux2 mux2_3 (.e0(mux2_1_out_4), .i(i1), .e1(mux2_2_out_4), .out_4(out_7));

  // Notes on the sheet:
  //   Ex4/Q1  La taille du sélecteur doit etre 2 bits
  //   Ex4/Q2   s = e0*n(i1)*n(i2) + e1*n(i1)*i2 + e2*i1*n(i2) + e3*i1*i2
  //   = n(i1)*(e0*n(i2) + e1*i2) + i1*(e2*n(i2) + e3*i2)
  //   = n(i1)*(n(i2)*e0 + i2*e1) + i1*(n(i2)*e2 + i2*e3)
  //   Ex4/Q3  Pour construire un multiplexeur à 2**n entrées à partir de multiplexeurs à 2 entrées, il faut juste utiliser n multiplexeurs à deux entrées.
endmodule

module comparaison (
  input  b2,
  input  b1,
  input  b0,
  input  a2,
  input  a1,
  input  a0,
  output out_7
);

  wire and_1_out, and_2_out, ex1_question1_1_a_et_non_b, ex1_question1_2_a_et_non_b,
       ex1_question1_3_a_et_non_b, mon_xor_1_out_3, mon_xor_2_out_3, not_1_out, not_2_out, or_1_out;

  Ex1_Question1 ex1_question1_1 (.a(b2), .b(a2), .a_ET_NON_b(ex1_question1_1_a_et_non_b));
  Ex1_Question1 ex1_question1_2 (.a(b0), .b(a0), .a_ET_NON_b(ex1_question1_2_a_et_non_b));
  Ex1_Question1 ex1_question1_3 (.a(b1), .b(a1), .a_ET_NON_b(ex1_question1_3_a_et_non_b));
  mon_xor mon_xor_1 (.a(b1), .b(a1), .out_3(mon_xor_1_out_3));
  not not_1 (not_1_out, mon_xor_1_out_3);
  mon_xor mon_xor_2 (.a(b2), .b(a2), .out_3(mon_xor_2_out_3));
  and and_1 (and_1_out, not_1_out, ex1_question1_2_a_et_non_b);
  not not_2 (not_2_out, mon_xor_2_out_3);
  or or_1 (or_1_out, ex1_question1_3_a_et_non_b, and_1_out);
  and and_2 (and_2_out, not_2_out, or_1_out);
  or or_2 (out_7, ex1_question1_1_a_et_non_b, and_2_out);

  // Notes on the sheet:
  //   Ex5/Q2    bi < ai = not(bi)*ai  
  //   bi > ai = ai*not(bi)
  //   bi = ai = not(a XOR b)
  //   Ex5/Q1   B>A = (b2>a2) + (b2=a2)*( (b1>a1) + (b1=a1)*(b0>a0) )
endmodule
